# Fritzing sketch r2d2_full (saved by Fritzing 0.7.12b)

parts:
  Arduino_Micro1 = Arduino Micro
  LED1 = RGB LED (com. anode, rbg) [package="5 mm [THT]"]
  S1 = Pushbutton [package="[THT]"]
  R1 = Resistor [tolerance=±5% resistance=10k package=THT]
  J1 = Piezo Speaker
  J2 = Basic Servo
  R2 = Resistor [tolerance=±5% resistance=220 package=THT]

nets:
  +5V: Arduino_Micro1.+5V, Arduino_Micro1.RESET, S1.Pin_2, J2.vcc
  GND: Arduino_Micro1.GND, Arduino_Micro1.Vin, R1.Pin_1, J1.pin1, J2.gnd, R2.Pin_0
  N1: Arduino_Micro1.D7, LED1.red_cathode
  N2: Arduino_Micro1.D8, LED1.blue_cathode
  N3: Arduino_Micro1.D9, LED1.green_cathode
  N4: Arduino_Micro1.D10, J2.pulse
  N5: Arduino_Micro1.D11, J1.pin2
  N6: Arduino_Micro1.D12, S1.Pin_3, S1.Pin_4, R1.Pin_0

custom parts:
  Arduino Micro: The awesome Arduino microcontroller
